# Fritzing sketch Arduino-IJbotma-Layout (saved by Fritzing 0.9.2b)
breadboards: 1

parts:
  R1 = Trimmer Potentiometer [maximum_resistance=10kΩ package=THT]
  LCD1 = LCD screen
  Part1 = Arduino Uno (Rev3)
  R2 = Resistor [tolerance=±5% resistance=220 package=THT]
  S1 = Pushbutton [package="[THT]"]
  R3 = Resistor [tolerance=±5% resistance=10k package=THT]

nets:
  VDD: R1.leg1, LCD1.VDD, Part1.5V, R2.Pin_1, S1.Pin_1, S1.Pin_2
  N1: R1.wiper, LCD1.V0
  VSS: R1.leg2, LCD1.VSS, LCD1.R/W, LCD1.LED-, Part1.GND, R3.Pin_1
  N2: LCD1.RS, Part1.D12/MISO
  N3: LCD1.E, Part1.D11_PWM/MOSI
  N4: LCD1.DB4, Part1.D5_PWM
  N5: LCD1.DB5, Part1.D4
  N6: LCD1.DB6, Part1.D3_PWM
  N7: LCD1.DB7, Part1.D2
  N8: LCD1.LED+, R2.Pin_0
  N9: Part1.D13/SCK, S1.Pin_3, S1.Pin_4, R3.Pin_0
